// Logisim project circuit.circ as structural Verilog: 8 circuits, main circuit main
module main (
);

  wire ALU_immediate, clock, condition_met, jump_enable, memory_read_enable, memory_write_enable,
       negate_output, register_write_enable, register_write_enable_2;
  wire [3:0] i0, i1, i2, i3;
  wire [15:0] ALU_result, data_memory_out, multiplexer_1_out, PC, register_out_i1, register_out_i2,
       register_out_i3;

  Clock clock_1 (.out(clock));
  signal_decoder signal_decoder_1 (
    .i0(i0), .jump_enable(jump_enable), .memory_read_enable(memory_read_enable),
    .ALU_immediate(ALU_immediate), .register_write_enable(register_write_enable),
    .register_write_enable_2(register_write_enable_2), .memory_write_enable(memory_write_enable),
    .negate_output(negate_output));
  program_counter program_counter_1 (
    .i1(i1), .condition_met(condition_met), .jump_enable(jump_enable), .clock(clock), .data(PC));
  instruction_memory instruction_memory_1 (.read_address(PC), .clock(clock), .i3(i3), .i2(i2), .i1(i1), .i0(i0));
  register_file register_file_1 (
    .clock(clock), .register_write_enable(register_write_enable), .i1(i1),
    .register_write_enable_2(register_write_enable_2), .i2(i2), .i3(i3), .write_data_1(data_memory_out),
    .write_data_2(ALU_result), .out_i1(register_out_i1), .out_i2(register_out_i2), .out_i3(register_out_i3));
  Multiplexer #(.width(16), .enable("false")) multiplexer_1 (
    .in0(register_out_i1), .in1(register_out_i2), .out(multiplexer_1_out), .sel(register_write_enable_2));
  ALU alu_1 (
    .operand_1(register_out_i2), .operand2(register_out_i3), .i0(i0), .negate_output(negate_output), .i3(i3),
    .ALU_immediate(ALU_immediate), .result(ALU_result), .condition_met(condition_met));
  data_memory data_memory_1 (
    .address(ALU_result), .write_enable(memory_write_enable), .read_enable(memory_read_enable),
    .clock(clock), .write_data(multiplexer_1_out), .data(data_memory_out));
endmodule

// PC
module program_counter (
  input  [3:0] i1,
  input  condition_met,
  input  clock,
  input  jump_enable,
  output [15:0] data
);

  wire and_1_out;
  wire [15:0] adder_1_out, adder_2_out, bit_extender_1_out, multiplexer_1_out;

  assign bit_extender_1_out = {{12{i1[3]}}, i1};  // Bit_Extender bit_extender_1
  Adder #(.width(16)) adder_1 (.a(data), .b(16'h1), .out(adder_1_out));  // open: cin, cout
  Adder #(.width(16)) adder_2 (.a(data), .b(bit_extender_1_out), .out(adder_2_out));  // open: cin, cout
  Multiplexer #(.width(16), .enable("false")) multiplexer_1 (
    .in0(adder_1_out), .in1(adder_2_out), .out(multiplexer_1_out), .sel(and_1_out));
  and and_1 (and_1_out, condition_met, jump_enable);
  Register #(.width(16), .trigger("falling")) PC (
    .D(multiplexer_1_out), .en(1'b1), .clk(clock), .Q(data));  // open: clr
endmodule

// IM
module instruction_memory (
  input  [15:0] read_address,
  input  clock,
  output [3:0] i3,
  output [3:0] i2,
  output [3:0] i1,
  output [3:0] i0
);

  RAM #(.addrWidth(16), .dataWidth(16), .databus("bibus")) IM (
    .addr(read_address), .we(1'b0), .oe(1'b1), .clk(clock), .dout({i0, i1, i2, i3}));  // open: din
endmodule

// Decoder
module signal_decoder (
  input  [3:0] i0,
  output jump_enable,
  output memory_read_enable,
  output ALU_immediate,
  output register_write_enable,
  output register_write_enable_2,
  output memory_write_enable,
  output negate_output
);

  wire and_1_out, and_2_out, and_3_out, and_4_out, and_5_out, and_7_out, and_8_out, and_9_out, and_11_out;

  and and_1 (and_1_out, i0[2], i0[3]);
  and and_2 (and_2_out, i0[0], i0[1], i0[3]);
  and and_3 (and_3_out, ~i0[0], ~i0[1], i0[3]);  // AND_Gate
  and and_4 (and_4_out, ~i0[1], ~i0[2]);  // AND_Gate
  and and_5 (and_5_out, ~i0[0], ~i0[1], ~i0[3]);  // AND_Gate
  and and_6 (memory_read_enable, i0[0], i0[3]);
  and and_7 (and_7_out, ~i0[2], ~i0[3]);  // AND_Gate
  and and_8 (and_8_out, ~i0[0], i0[1], i0[3]);  // AND_Gate
  and and_9 (and_9_out, i0[0], i0[2]);
  and and_10 (negate_output, ~i0[0], ~i0[1], ~i0[2], ~i0[3]);  // AND_Gate
  and and_11 (and_11_out, i0[1], i0[2]);
  or or_1 (jump_enable, and_9_out, and_11_out);
  or or_2 (ALU_immediate, and_1_out, and_3_out, and_2_out);
  or or_3 (register_write_enable, and_4_out, and_5_out, and_7_out, memory_read_enable);
  or or_4 (register_write_enable_2, and_1_out, and_2_out);
  or or_5 (memory_write_enable, and_1_out, and_8_out);
endmodule

// RF
module register_file (
  input  [3:0] i1,
  input  register_write_enable,
  input  [3:0] i2,
  input  register_write_enable_2,
  input  clock,
  input  [3:0] i3,
  input  [15:0] write_data_1,
  input  [15:0] write_data_2,
  output [15:0] out_i1,
  output [15:0] out_i2,
  output [15:0] out_i3
);

  wire altsrc1, altsrc2, altsrc3, altsrc4, altsrc5, altsrc6, altsrc7, altsrc8, altsrc9, altsrc10, altsrc11,
       altsrc12, altsrc13, altsrc14, altsrc15, decoder_1_out1, decoder_1_out2, decoder_1_out3,
       decoder_1_out4, decoder_1_out5, decoder_1_out6, decoder_1_out7, decoder_1_out8, decoder_1_out9,
       decoder_1_out10, decoder_1_out11, decoder_1_out12, decoder_1_out13, decoder_1_out14, decoder_1_out15,
       WE1, WE2, WE3, WE4, WE5, WE6, WE7, WE8, WE9, WE10, WE11, WE12, WE13, WE14, WE15;
  wire [15:0] multiplexer_1_out, multiplexer_2_out, multiplexer_3_out, multiplexer_4_out, multiplexer_5_out,
       multiplexer_6_out, multiplexer_7_out, multiplexer_8_out, multiplexer_9_out, multiplexer_10_out,
       multiplexer_11_out, multiplexer_12_out, multiplexer_13_out, multiplexer_14_out, multiplexer_15_out,
       Q0, Q1, Q2, Q3, Q4, Q5, Q6, Q7, Q8, Q9, Q10, Q11, Q12, Q13, Q14, Q15;

  Decoder #(.select(4)) decoder_1 (
    .out1(decoder_1_out1), .out2(decoder_1_out2), .out3(decoder_1_out3), .out4(decoder_1_out4),
    .out5(decoder_1_out5), .out6(decoder_1_out6), .out7(decoder_1_out7), .out8(decoder_1_out8),
    .out9(decoder_1_out9), .out10(decoder_1_out10), .out11(decoder_1_out11), .out12(decoder_1_out12),
    .out13(decoder_1_out13), .out14(decoder_1_out14), .out15(decoder_1_out15), .sel(i1),
    .en(register_write_enable));  // open: out0
  Decoder #(.select(4)) decoder_2 (
    .out1(altsrc1), .out2(altsrc2), .out3(altsrc3), .out4(altsrc4), .out5(altsrc5), .out6(altsrc6),
    .out7(altsrc7), .out8(altsrc8), .out9(altsrc9), .out10(altsrc10), .out11(altsrc11), .out12(altsrc12),
    .out13(altsrc13), .out14(altsrc14), .out15(altsrc15), .sel(i2), .en(register_write_enable_2));  // open: out0
  or or_1 (WE1, decoder_1_out1, altsrc1);
  or or_2 (WE2, decoder_1_out2, altsrc2);
  or or_3 (WE3, decoder_1_out3, altsrc3);
  or or_4 (WE4, decoder_1_out4, altsrc4);
  or or_5 (WE5, decoder_1_out5, altsrc5);
  or or_6 (WE6, decoder_1_out6, altsrc6);
  or or_7 (WE7, decoder_1_out7, altsrc7);
  or or_8 (WE8, decoder_1_out8, altsrc8);
  or or_9 (WE9, decoder_1_out9, altsrc9);
  or or_10 (WE10, decoder_1_out10, altsrc10);
  or or_11 (WE11, decoder_1_out11, altsrc11);
  or or_12 (WE12, decoder_1_out12, altsrc12);
  or or_13 (WE13, decoder_1_out13, altsrc13);
  or or_14 (WE14, decoder_1_out14, altsrc14);
  or or_15 (WE15, decoder_1_out15, altsrc15);
  Register #(.width(16), .trigger("falling")) register_1 (.Q(Q0));  // open: D, en, clk, clr
  Register #(.width(16), .trigger("falling")) register_2 (
    .D(multiplexer_1_out), .en(WE1), .clk(clock), .Q(Q1));  // open: clr
  Multiplexer #(.width(16), .enable("false")) multiplexer_1 (
    .in0(write_data_1), .in1(write_data_2), .out(multiplexer_1_out), .sel(altsrc1));
  Register #(.width(16), .trigger("falling")) register_3 (
    .D(multiplexer_2_out), .en(WE2), .clk(clock), .Q(Q2));  // open: clr
  Multiplexer #(.width(16), .enable("false")) multiplexer_2 (
    .in0(write_data_1), .in1(write_data_2), .out(multiplexer_2_out), .sel(altsrc2));
  Register #(.width(16), .trigger("falling")) register_4 (
    .D(multiplexer_3_out), .en(WE3), .clk(clock), .Q(Q3));  // open: clr
  Multiplexer #(.width(16), .enable("false")) multiplexer_3 (
    .in0(write_data_1), .in1(write_data_2), .out(multiplexer_3_out), .sel(altsrc3));
  Register #(.width(16), .trigger("falling")) register_5 (
    .D(multiplexer_4_out), .en(WE4), .clk(clock), .Q(Q4));  // open: clr
  Multiplexer #(.width(16), .enable("false")) multiplexer_4 (
    .in0(write_data_1), .in1(write_data_2), .out(multiplexer_4_out), .sel(altsrc4));
  Register #(.width(16), .trigger("falling")) register_6 (
    .D(multiplexer_5_out), .en(WE5), .clk(clock), .Q(Q5));  // open: clr
  Multiplexer #(.width(16), .enable("false")) multiplexer_5 (
    .in0(write_data_1), .in1(write_data_2), .out(multiplexer_5_out), .sel(altsrc5));
  Register #(.width(16), .trigger("falling")) register_7 (
    .D(multiplexer_6_out), .en(WE6), .clk(clock), .Q(Q6));  // open: clr
  Multiplexer #(.width(16), .enable("false")) multiplexer_6 (
    .in0(write_data_1), .in1(write_data_2), .out(multiplexer_6_out), .sel(altsrc6));
  Register #(.width(16), .trigger("falling")) register_8 (
    .D(multiplexer_7_out), .en(WE7), .clk(clock), .Q(Q7));  // open: clr
  Multiplexer #(.width(16), .enable("false")) multiplexer_7 (
    .in0(write_data_1), .in1(write_data_2), .out(multiplexer_7_out), .sel(altsrc7));
  Register #(.width(16), .trigger("falling")) register_9 (
    .D(multiplexer_8_out), .en(WE8), .clk(clock), .Q(Q8));  // open: clr
  Multiplexer #(.width(16), .enable("false")) multiplexer_8 (
    .in0(write_data_1), .in1(write_data_2), .out(multiplexer_8_out), .sel(altsrc8));
  Register #(.width(16), .trigger("falling")) register_10 (
    .D(multiplexer_9_out), .en(WE9), .clk(clock), .Q(Q9));  // open: clr
  Multiplexer #(.width(16), .enable("false")) multiplexer_9 (
    .in0(write_data_1), .in1(write_data_2), .out(multiplexer_9_out), .sel(altsrc9));
  Register #(.width(16), .trigger("falling")) register_11 (
    .D(multiplexer_10_out), .en(WE10), .clk(clock), .Q(Q10));  // open: clr
  Multiplexer #(.width(16), .enable("false")) multiplexer_10 (
    .in0(write_data_1), .in1(write_data_2), .out(multiplexer_10_out), .sel(altsrc10));
  Register #(.width(16), .trigger("falling")) register_12 (
    .D(multiplexer_11_out), .en(WE11), .clk(clock), .Q(Q11));  // open: clr
  Multiplexer #(.width(16), .enable("false")) multiplexer_11 (
    .in0(write_data_1), .in1(write_data_2), .out(multiplexer_11_out), .sel(altsrc11));
  Register #(.width(16), .trigger("falling")) register_13 (
    .D(multiplexer_12_out), .en(WE12), .clk(clock), .Q(Q12));  // open: clr
  Multiplexer #(.width(16), .enable("false")) multiplexer_12 (
    .in0(write_data_1), .in1(write_data_2), .out(multiplexer_12_out), .sel(altsrc12));
  Register #(.width(16), .trigger("falling")) register_14 (
    .D(multiplexer_13_out), .en(WE13), .clk(clock), .Q(Q13));  // open: clr
  Multiplexer #(.width(16), .enable("false")) multiplexer_13 (
    .in0(write_data_1), .in1(write_data_2), .out(multiplexer_13_out), .sel(altsrc13));
  Register #(.width(16), .trigger("falling")) register_15 (
    .D(multiplexer_14_out), .en(WE14), .clk(clock), .Q(Q14));  // open: clr
  Multiplexer #(.width(16), .enable("false")) multiplexer_14 (
    .in0(write_data_1), .in1(write_data_2), .out(multiplexer_14_out), .sel(altsrc14));
  Register #(.width(16), .trigger("falling")) register_16 (
    .D(multiplexer_15_out), .en(WE15), .clk(clock), .Q(Q15));  // open: clr
  Multiplexer #(.width(16), .enable("false")) multiplexer_15 (
    .in0(write_data_1), .in1(write_data_2), .out(multiplexer_15_out), .sel(altsrc15));
  Multiplexer #(.select(4), .width(16), .enable("false")) multiplexer_16 (
    .in0(Q0), .in1(Q1), .in2(Q2), .in3(Q3), .in4(Q4), .in5(Q5), .in6(Q6), .in7(Q7), .in8(Q8), .in9(Q9),
    .in10(Q10), .in11(Q11), .in12(Q12), .in13(Q13), .in14(Q14), .in15(Q15), .out(out_i1), .sel(i1));
  Multiplexer #(.select(4), .width(16), .enable("false")) multiplexer_17 (
    .in0(Q0), .in1(Q1), .in2(Q2), .in3(Q3), .in4(Q4), .in5(Q5), .in6(Q6), .in7(Q7), .in8(Q8), .in9(Q9),
    .in10(Q10), .in11(Q11), .in12(Q12), .in13(Q13), .in14(Q14), .in15(Q15), .out(out_i2), .sel(i2));
  Multiplexer #(.select(4), .width(16), .enable("false")) multiplexer_18 (
    .in0(Q0), .in1(Q1), .in2(Q2), .in3(Q3), .in4(Q4), .in5(Q5), .in6(Q6), .in7(Q7), .in8(Q8), .in9(Q9),
    .in10(Q10), .in11(Q11), .in12(Q12), .in13(Q13), .in14(Q14), .in15(Q15), .out(out_i3), .sel(i3));
endmodule

module ALU (
  input  [15:0] operand_1,
  input  [15:0] operand2,
  input  [3:0] i0,
  input  negate_output,
  input  [3:0] i3,
  input  ALU_immediate,
  output [15:0] result,
  output condition_met
);

  wire and_1_out, and_2_out, and_3_out, and_4_out, and_6_out, and_7_out, and_8_out, and_9_out, and_10_out,
       and_11_out, comparator_1_eq, comparator_1_gt, comparator_1_lt, not_1_out;
  wire [1:0] or_1_out;
  wire [15:0] adder_1_out, and_5_out, bit_extender_1_out, multiplexer_1_out, multiplexer_2_out, not_2_out,
       or_3_out, subtractor_1_out;

  Multiplexer #(.width(16), .enable("false")) multiplexer_1 (
    .in0(operand2), .in1(bit_extender_1_out), .out(multiplexer_1_out), .sel(ALU_immediate));
  assign bit_extender_1_out = {{12{i3[3]}}, i3};  // Bit_Extender bit_extender_1
  and and_1 (and_1_out, ~i0[0], i0[1], ~i0[2], ~i0[3]);  // AND_Gate
  and and_2 (and_2_out, ~i0[0], ~i0[1], i0[2], ~i0[3]);  // AND_Gate
  or or_1 (or_1_out[0], and_1_out, and_2_out);
  and and_3 (and_3_out, i0[0], i0[1], ~i0[2], ~i0[3]);  // AND_Gate
  and and_4 (and_4_out, ~i0[0], ~i0[1], i0[2], ~i0[3]);  // AND_Gate
  or or_2 (or_1_out[1], and_3_out, and_4_out);
  assign or_3_out = operand_1 | multiplexer_1_out;  // OR_Gate or_3, 16 bits wide
  assign and_5_out = operand_1 & multiplexer_1_out;  // AND_Gate and_5, 16 bits wide
  Adder #(.width(16)) adder_1 (.a(operand_1), .b(multiplexer_1_out), .out(adder_1_out));  // open: cin, cout
  Subtractor #(.width(16)) subtractor_1 (
    .a(operand_1), .b(multiplexer_1_out), .out(subtractor_1_out));  // open: bin, bout
  Comparator #(.width(16)) comparator_1 (
    .a(operand_1), .b(multiplexer_1_out), .gt(comparator_1_gt), .eq(comparator_1_eq), .lt(comparator_1_lt));
  not not_1 (not_1_out, comparator_1_lt);
  and and_6 (and_6_out, ~i0[0], i0[1], i0[2], ~i0[3]);  // AND_Gate
  and and_7 (and_7_out, i0[0], ~i0[1], i0[2], ~i0[3]);  // AND_Gate
  Multiplexer #(.select(2), .width(16), .enable("false")) multiplexer_2 (
    .in0(adder_1_out), .in1(subtractor_1_out), .in2(or_3_out), .in3(and_5_out), .out(multiplexer_2_out),
    .sel(or_1_out));
  and and_8 (and_8_out, i0[0], i0[1], i0[2], ~i0[3]);  // AND_Gate
  Multiplexer #(.width(16), .enable("false")) multiplexer_3 (
    .in0(multiplexer_2_out), .in1(not_2_out), .out(result), .sel(negate_output));
  assign not_2_out = ~multiplexer_2_out;  // NOT_Gate not_2, 16 bits wide
  and and_9 (and_9_out, and_7_out, comparator_1_eq);
  and and_10 (and_10_out, and_6_out, comparator_1_gt);
  and and_11 (and_11_out, and_8_out, not_1_out);
  or or_4 (condition_met, and_9_out, and_10_out, and_11_out);
endmodule

// DM
module data_memory (
  input  [15:0] address,
  input  write_enable,
  input  read_enable,
  input  clock,
  input  [15:0] write_data,
  output [15:0] data
);

  wire [15:0] ram_1_dout;

  RAM #(.addrWidth(16), .dataWidth(16), .trigger("falling"), .databus("bibus")) ram_1 (
    .addr(address), .we(write_enable), .oe(read_enable), .clk(clock), .din(write_data), .dout(ram_1_dout));
  Multiplexer #(.width(16), .enable("false")) multiplexer_1 (
    .in0(address), .in1(ram_1_dout), .out(data), .sel(read_enable));
endmodule

module testing (
);

  wire and_1_out, clock_1_out, memory_read_enable;
  wire [7:0] ram_1_dout, ram_2_dout, undriven;
  wire [15:0] not_1_out, undriven_2, undriven_3;

  Clock clock_1 (.out(clock_1_out));
  RAM #(.addrWidth(16), .trigger("high"), .databus("bibus")) ram_1 (
    .addr(undriven_3), .we(and_1_out), .oe(memory_read_enable), .dout(ram_1_dout));  // open: din
  assign not_1_out = ~undriven_2;  // NOT_Gate not_1, 16 bits wide
  buf and_1 (and_1_out, ~clock_1_out);  // AND_Gate AND_Gate
  RAM #(.addrWidth(16), .trigger("high"), .databus("bibus")) ram_2 (
    .addr(undriven_2), .we(and_1_out), .oe(memory_read_enable), .din(undriven), .dout(ram_2_dout));
endmodule
